# Fritzing sketch pcb10_smd (saved by Fritzing 0.8.7b)
circuit board: 4.62cm x 7.5cm
breadboards: 3

parts:
  Raspberry_Pi_B_rev1 = Raspberry Pi B rev2
  S1 = Pushbutton [package="[SMD]"]
  M1 = DC Motor
  Q1 = PHOTOTRANSISTOR REFLECTIVE OBJECT SENSOR [package=qrb1114-side]
  LED2 = LED - 5mm [color="Red (633nm)" package="5 mm [THT]"]
  R12 = Resistor [tolerance=±5% resistance=6.8 power=2W package=THT]
  D2 = Diode [package=diode-1n4001]
  C1 = Electrolytic Capacitor [capacitance=100μF voltage=16V package="100 mil [THT, electrolytic]"]
  AMPIN = male pin header, 2 pins [form="♂ (male)"]
  IRSEN = male pin header, 3 pins [form="♂ (male)"]
  MCP3002 = IC, DIP package, 8 pins [chip_label=MCP3002]
  MOTOR = male pin header, 2 pins [form="♂ (male)"]
  AMPOUT = male pin header, 2 pins [form="♂ (male)"]
  LEDSW = male pin header, 3 pins [form="♂ (male)"]
  Power_plug1 = Power plug
  C2 = Electrolytic Capacitor [capacitance=1mF package="200 mil [THT, electrolytic]"]
  L293D = IC, DIP package, 16 pins [chip_label=L293D]
  LM2576-5 = mystery part, 5 pins [chip_label=?]
  C4 = Electrolytic Capacitor [capacitance=10µF package="0605 [SMD, electrolytic]"]
  C5 = Electrolytic Capacitor [capacitance=220µF voltage=10V package="0605 [SMD, electrolytic]"]
  L5 = Inductors [part_number=300uh package=sru1038]
  LM386 = IC, DIP package, 8 pins [chip_label=IC]
  R7 = Resistor [tolerance=±5% resistance=470 package="0805 [SMD]"]
  R8 = Resistor [tolerance=±5% resistance=22k package="0603 [SMD]"]
  R11 = Resistor [tolerance=±5% resistance=4.99k package="0603 [SMD]"]
  R10 = Resistor [tolerance=±5% resistance=15k package="0603 [SMD]"]
  R9 = Resistor [tolerance=±5% resistance=470 package="0805 [SMD]"]
  C8 = Ceramic Capacitor [capacitance=10nF package="0603 [SMD, multilayer]"]
  R14 = Resistor [tolerance=±5% resistance=100 package="0805 [SMD]"]
  C6 = Ceramic Capacitor [capacitance=47nF voltage=16V package="0603 [SMD, multilayer]"]
  C3 = Ceramic Capacitor [capacitance=100nF package="0603 [SMD, multilayer]"]
  R13 = Resistor [tolerance=±5% resistance=100k package="0603 [SMD]"]
  R16 = Resistor [tolerance=±5% resistance=15k package="0603 [SMD]"]
  R15 = Resistor [tolerance=±5% resistance=1k package="0603 [SMD]"]
  U1 = DIODE-ZENER [package=sod-323]
  C7 = Electrolytic Capacitor [capacitance=10µF package="0605 [SMD, electrolytic]"]

nets:
  3.3V: Raspberry_Pi_B_rev1.3V3, MCP3002.pin8, R7.Pin_1, R8.Pin_1
  5V: Raspberry_Pi_B_rev1.5V, C2.+, L293D.pin16, LM2576-5.pin4, L5.2, LM386.pin6
  GPIO3: Raspberry_Pi_B_rev1.GPIO_3, S1.Pin_1, S1.Pin_2, LEDSW.pin1
  GND: Raspberry_Pi_B_rev1.GND, S1.Pin_3, S1.Pin_4, Q1.E, Q1.K, LED2.cathode, C1.-, AMPIN.pin2, IRSEN.pin1, MCP3002.pin4, AMPOUT.pin2, LEDSW.pin2, Power_plug1.GND, C2.-, L293D.pin1, L293D.pin2, L293D.pin3, L293D.pin4, L293D.pin5, L293D.pin6, L293D.pin7, L293D.pin12, L293D.pin13, LM2576-5.pin3, LM2576-5.pin5, C4.-, LM386.pin2, LM386.pin4, R11.Pin_1, C8.1, R14.Pin_0, R16.Pin_0, U1.C
  GPIO27: Raspberry_Pi_B_rev1.GPIO_27, L293D.pin10
  GPIO22: Raspberry_Pi_B_rev1.GPIO_22, L293D.pin9
  GPIO4: Raspberry_Pi_B_rev1.GPIO_4, R9.Pin_1
  GPIO10: Raspberry_Pi_B_rev1.GPIO_10, MCP3002.pin5
  GPIO9: Raspberry_Pi_B_rev1.GPIO_9, MCP3002.pin6
  GPIO11: Raspberry_Pi_B_rev1.GPIO_11, MCP3002.pin7
  GPIO8: Raspberry_Pi_B_rev1.GPIO_8, MCP3002.pin1
  GPIO7: Raspberry_Pi_B_rev1.GPIO_7, L293D.pin15
  N1: M1.pin_1, MOTOR.pin2, L293D.pin14
  N2: M1.pin_2, MOTOR.pin1, L293D.pin11
  N3: Q1.A, IRSEN.pin2, R7.Pin_0
  AD1: Q1.C, IRSEN.pin3, MCP3002.pin2, R8.Pin_0
  N4: LED2.anode, LEDSW.pin3, R9.Pin_0
  12V: R12.Pin_0, D2.C, C1.+, Power_plug1.VCC
  N5: R12.Pin_1, L293D.pin8, R10.Pin_0
  N6: D2.A, LM2576-5.pin1
  N7: AMPIN.pin1, R13.Pin_1
  AD2: MCP3002.pin3, R11.Pin_0, R10.Pin_1
  N8: AMPOUT.pin1, C5.-
  N9: LM2576-5.pin2, L5.1, U1.A
  N10: C4.+, LM386.pin7
  Vout: C5.+, LM386.pin5, C6.0
  N11: LM386.pin1, C7.+
  +IN: LM386.pin3, C8.0, C3.0, R16.Pin_1
  N12: LM386.pin8, R15.Pin_1
  N13: R14.Pin_1, C6.1
  N14: C3.1, R13.Pin_0
  N15: R15.Pin_0, C7.-

notes:
  PB.v10
  PetBot, 12V to 5V switching power supply
  PetBot, Motor driver
  PetBot, Amplifier for PetBot
  PetBot, LED and switch
  PetBot, Analog to digtial
  PetBot, Raspberry pi
  PetBot, IR sensor
