# Fritzing sketch pcb11 (saved by Fritzing 0.8.7b)
breadboards: 3

parts:
  Raspberry_Pi_B_rev1 = Raspberry Pi B rev2
  S1 = Pushbutton [package="[SMD]"]
  M1 = DC Motor
  Q1 = PHOTOTRANSISTOR REFLECTIVE OBJECT SENSOR [package=qrb1114-side]
  LED2 = LED - 5mm [color="Red (633nm)" package="5 mm [THT]"]
  R12 = Resistor [tolerance=±5% resistance=6.8 power=2W package=THT]
  D2 = Diode [package=diode-1n4001]
  AIN = male pin header, 2 pins [form="♂ (male)"]
  IR = male pin header, 3 pins [form="♂ (male)"]
  AOUT = male pin header, 2 pins [form="♂ (male)"]
  Power_plug1 = Power plug
  L293D = IC, DIP package, 16 pins [chip_label=L293D]
  C5 = Electrolytic Capacitor [capacitance=220µF voltage=10V package="0605 [SMD, electrolytic]"]
  POL5v = mystery part, 3 pins [chip_label=?]
  C9 = Ceramic Capacitor [capacitance=10µF package="1206 [SMD, multilayer]"]
  MCP3002 = SO08 [chip_label=MCP3002 package=SO]
  C10 = Ceramic Capacitor [capacitance=10µF package="1206 [SMD, multilayer]"]
  LM386 = SO08 [chip_label=IC package=SO]
  R11 = Resistor [tolerance=±5% resistance=4.99k package="0603 [SMD]"]
  R7 = Resistor [tolerance=±5% resistance=470 package="0805 [SMD]"]
  R8 = Resistor [tolerance=±5% resistance=22k package="0603 [SMD]"]
  R15 = Resistor [tolerance=±5% resistance=1k package="0603 [SMD]"]
  R10 = Resistor [tolerance=±5% resistance=15k package="0603 [SMD]"]
  R14 = Resistor [tolerance=±5% resistance=100 package="0805 [SMD]"]
  C8 = Ceramic Capacitor [capacitance=10nF package="0603 [SMD, multilayer]"]
  C6 = Ceramic Capacitor [capacitance=47nF voltage=16V package="0603 [SMD, multilayer]"]
  R16 = Resistor [tolerance=±5% resistance=15k package="0603 [SMD]"]
  R13 = Resistor [tolerance=±5% resistance=100k package="0603 [SMD]"]
  C3 = Ceramic Capacitor [capacitance=100nF package="0603 [SMD, multilayer]"]
  M4 = DC Motor
  LS = male pin header, 6 pins [form="♂ (male)"]
  R17 = Resistor [tolerance=±5% resistance=270 package="0603 [SMD]"]
  R18 = Resistor [tolerance=±5% resistance=270 package="0603 [SMD]"]
  R19 = Resistor [tolerance=±5% resistance=270 package="0603 [SMD]"]
  R9 = Resistor [tolerance=±5% resistance=270 package="0603 [SMD]"]

nets (from the breadboard view):
  N1: Raspberry_Pi_B_rev1.3V3, MCP3002.8, R7.Pin_1, R8.Pin_1
  N2: Raspberry_Pi_B_rev1.5V, L293D.pin16, POL5v.pin3, LM386.6
  N3: Raspberry_Pi_B_rev1.GPIO_3, S1.Pin_2, LS.pin1
  GND: Raspberry_Pi_B_rev1.GND, S1.Pin_4, Q1.E, Q1.K, LED2.cathode, AIN.pin2, IR.pin1, AOUT.pin2, Power_plug1.GND, L293D.pin1, L293D.pin4, L293D.pin5, L293D.pin12, L293D.pin13, POL5v.pin2, MCP3002.4, LM386.4, R11.Pin_1, R14.Pin_0, LS.pin2
  N4: Raspberry_Pi_B_rev1.GPIO_23, R18.Pin_0
  N5: Raspberry_Pi_B_rev1.GPIO_15, R17.Pin_0
  N6: Raspberry_Pi_B_rev1.GPIO_17, L293D.pin7
  N7: Raspberry_Pi_B_rev1.GPIO_18, L293D.pin2
  N8: Raspberry_Pi_B_rev1.GPIO_27, L293D.pin10
  N9: Raspberry_Pi_B_rev1.GPIO_22, L293D.pin9
  N10: Raspberry_Pi_B_rev1.GPIO_4, R9.Pin_1
  N11: Raspberry_Pi_B_rev1.GPIO_10, MCP3002.5
  N12: Raspberry_Pi_B_rev1.GPIO_9, MCP3002.6
  N13: Raspberry_Pi_B_rev1.GPIO_25, R19.Pin_0
  N14: Raspberry_Pi_B_rev1.GPIO_11, MCP3002.7
  N15: Raspberry_Pi_B_rev1.GPIO_8, MCP3002.1
  N16: Raspberry_Pi_B_rev1.GPIO_7, L293D.pin15
  N17: M1.pin_1, L293D.pin14
  N18: M1.pin_2, L293D.pin11
  N19: Q1.A, IR.pin2, R7.Pin_0
  N20: Q1.C, IR.pin3, MCP3002.2, R8.Pin_0
  N21: LED2.anode, LS.pin3, R9.Pin_0
  N22: R12.Pin_0, D2.C, Power_plug1.VCC
  N23: R12.Pin_1, L293D.pin8, R10.Pin_0
  N24: D2.A, POL5v.pin1
  N25: AIN.pin1, R13.Pin_1
  N26: AOUT.pin1, C5.-
  N27: L293D.pin3, M4.pin_1
  N28: L293D.pin6, M4.pin_2
  N29: C5.+, LM386.5, C6.0
  N30: C9.0, LM386.2, C8.1, R16.Pin_0
  N31: C9.1, LM386.7
  N32: MCP3002.3, R11.Pin_0, R10.Pin_1
  N33: C10.0, LM386.1
  N34: C10.1, R15.Pin_0
  N35: LM386.3, C8.0, R16.Pin_1, C3.0
  N36: LM386.8, R15.Pin_1
  N37: R14.Pin_1, C6.1
  N38: R13.Pin_0, C3.1
  N39: LS.pin4, R17.Pin_1
  N40: LS.pin5, R18.Pin_1
  N41: LS.pin6, R19.Pin_1

notes:
  PB.v11
  PetBot, 12V to 5V switching power supply
  PetBot, Motor driver
  PetBot, Amplifier for PetBot
  PetBot, LED and switch
  PetBot, Analog to digtial
  PetBot, Raspberry pi
  PetBot, IR sensor
