# Fritzing sketch pcb9 (saved by Fritzing 0.8.7b)
circuit board: 4.65316cm x 8.36371cm
breadboards: 3

parts:
  Raspberry_Pi_B_rev1 = Raspberry Pi B rev2
  S1 = Pushbutton [package="[SMD]"]
  M1 = DC Motor
  Q1 = PHOTOTRANSISTOR REFLECTIVE OBJECT SENSOR [package=qrb1114-side]
  LED2 = LED - 5mm [color="Red (633nm)" package="5 mm [THT]"]
  R12 = Resistor [tolerance=±5% resistance=56 power=2W package=THT]
  LM2576-5 = mystery part, 5 pins [chip_label=?]
  L1 = Inductor [inductance=100µH current=1.5A package="400 mil [THT]"]
  D2 = Diode [package=diode-1n4001]
  C1 = Electrolytic Capacitor [capacitance=100μF voltage=16V package="100 mil [THT, electrolytic]"]
  R13 = Resistor [tolerance=±5% resistance=100k package=THT]
  D1 = Schottky Diode [part_number=1N5817 package="300 mil [THT]"]
  AMPIN = male pin header, 2 pins [form="♂ (male)"]
  C3 = Ceramic Capacitor [capacitance=100nF package="100 mil [THT, multilayer]"]
  C4 = Electrolytic Capacitor [capacitance=1µF package="100 mil [THT, electrolytic]"]
  LM386 = LM386 [package=dip08]
  R7 = Resistor [tolerance=±5% resistance=470 package=THT]
  R8 = Resistor [tolerance=±5% resistance=22k package=THT]
  IRSEN = male pin header, 3 pins [form="♂ (male)"]
  MCP3002 = IC, DIP package, 8 pins [chip_label=MCP3002]
  LM294 = IC, DIP package, 16 pins [chip_label=LM293]
  MOTOR = male pin header, 2 pins [form="♂ (male)"]
  R11 = Resistor [tolerance=±5% resistance=5k package=THT]
  R10 = Resistor [tolerance=±5% resistance=15k package=THT]
  AMPOUT = male pin header, 2 pins [form="♂ (male)"]
  C6 = Ceramic Capacitor [capacitance=100nF package="100 mil [THT, multilayer]"]
  C5 = Electrolytic Capacitor [capacitance=220µF package="100 mil [THT, electrolytic]"]
  LEDSW = male pin header, 3 pins [form="♂ (male)"]
  Power_plug1 = Power plug
  C7 = Electrolytic Capacitor [capacitance=10µF package="100 mil [THT, electrolytic]"]
  C8 = Ceramic Capacitor [capacitance=10nF package="100 mil [THT, multilayer]"]
  R16 = Resistor [tolerance=±5% resistance=15k package=THT]
  R15 = Resistor [tolerance=±5% resistance=1k package=THT]
  C2 = Electrolytic Capacitor [capacitance=1mF package="200 mil [THT, electrolytic]"]
  R14 = Resistor [tolerance=±5% resistance=100 package=THT]
  R9 = Resistor [tolerance=±5% resistance=220 package=THT]

nets:
  N1: Raspberry_Pi_B_rev1.3V3, R7.Pin_1, R8.Pin_1, MCP3002.pin8
  N2: Raspberry_Pi_B_rev1.5V, LM2576-5.pin4, L1.pin_1, LM386.V+, LM294.pin16, C2.+
  N3: Raspberry_Pi_B_rev1.GPIO_3, S1.Pin_2, LEDSW.pin1
  GND: Raspberry_Pi_B_rev1.GND, S1.Pin_3, S1.Pin_4, Q1.E, Q1.K, LED2.cathode, LM2576-5.pin3, LM2576-5.pin5, C1.-, D1.anode, AMPIN.pin2, LM386.V-, IRSEN.pin1, MCP3002.pin4, LM294.pin1, LM294.pin2, LM294.pin3, LM294.pin4, LM294.pin5, LM294.pin6, LM294.pin7, LM294.pin12, LM294.pin13, R11.Pin_1, AMPOUT.pin2, LEDSW.pin2, Power_plug1.GND, C2.-, R14.Pin_0
  N4: Raspberry_Pi_B_rev1.GPIO_27, LM294.pin10
  N5: Raspberry_Pi_B_rev1.GPIO_22, LM294.pin9
  N6: Raspberry_Pi_B_rev1.GPIO_4, R9.Pin_1
  N7: Raspberry_Pi_B_rev1.GPIO_10, MCP3002.pin5
  N8: Raspberry_Pi_B_rev1.GPIO_9, MCP3002.pin6
  N9: Raspberry_Pi_B_rev1.GPIO_11, MCP3002.pin7
  N10: Raspberry_Pi_B_rev1.GPIO_8, MCP3002.pin1
  N11: Raspberry_Pi_B_rev1.GPIO_7, LM294.pin15
  N12: M1.pin_1, LM294.pin14, MOTOR.pin2
  N13: M1.pin_2, LM294.pin11, MOTOR.pin1
  N14: Q1.A, R7.Pin_0, IRSEN.pin2
  N15: Q1.C, R8.Pin_0, IRSEN.pin3, MCP3002.pin2
  N16: LED2.anode, LEDSW.pin3, R9.Pin_0
  N17: R12.Pin_0, D2.C, C1.+, Power_plug1.VCC
  N18: R12.Pin_1, LM294.pin8, R10.Pin_0
  N19: LM2576-5.pin1, D2.A
  N20: LM2576-5.pin2, L1.pin_0, D1.cathode
  N21: R13.Pin_0, C3.1
  N22: R13.Pin_1, AMPIN.pin1
  N23: C3.0, LM386.+IN, C8.0, R16.Pin_1
  N24: C4.-, LM386.-IN, C8.1, R16.Pin_0
  N25: C4.+, LM386.BP
  N26: LM386.GAIN, C7.+, R15.Pin_1
  N27: LM386.OUT, C6.0, C5.+
  N28: MCP3002.pin3, R11.Pin_0, R10.Pin_1
  N29: AMPOUT.pin1, C5.-
  N30: C6.1, R14.Pin_1
  N31: C7.-, R15.Pin_0

notes:
  PB.v9
