# Fritzing sketch pcb9_smd (saved by Fritzing 0.8.7b)
circuit board: 4.619cm x 8.41411cm
breadboards: 3

parts:
  Raspberry_Pi_B_rev1 = Raspberry Pi B rev2
  S1 = Pushbutton [package="[SMD]"]
  M1 = DC Motor
  Q1 = PHOTOTRANSISTOR REFLECTIVE OBJECT SENSOR [package=qrb1114-side]
  LED2 = LED - 5mm [color="Red (633nm)" package="5 mm [THT]"]
  R12 = Resistor [tolerance=±5% resistance=56 power=2W package=THT]
  D2 = Diode [package=diode-1n4001]
  C1 = Electrolytic Capacitor [capacitance=100μF voltage=16V package="100 mil [THT, electrolytic]"]
  AMPIN = male pin header, 2 pins [form="♂ (male)"]
  C3 = Ceramic Capacitor [capacitance=100nF package="100 mil [THT, multilayer]"]
  C4 = Electrolytic Capacitor [capacitance=1µF package="100 mil [THT, electrolytic]"]
  LM386 = LM386 [package=dip08]
  IRSEN = male pin header, 3 pins [form="♂ (male)"]
  MCP3002 = IC, DIP package, 8 pins [chip_label=MCP3002]
  MOTOR = male pin header, 2 pins [form="♂ (male)"]
  AMPOUT = male pin header, 2 pins [form="♂ (male)"]
  C6 = Ceramic Capacitor [capacitance=100nF package="100 mil [THT, multilayer]"]
  C5 = Electrolytic Capacitor [capacitance=1µF package="100 mil [THT, electrolytic]"]
  LEDSW = male pin header, 3 pins [form="♂ (male)"]
  Power_plug1 = Power plug
  C7 = Electrolytic Capacitor [capacitance=10µF package="100 mil [THT, electrolytic]"]
  C8 = Ceramic Capacitor [capacitance=10nF package="100 mil [THT, multilayer]"]
  C2 = Electrolytic Capacitor [capacitance=1mF package="200 mil [THT, electrolytic]"]
  R15 = Resistor [tolerance=±5% resistance=1k package="0603 [SMD]"]
  R11 = Resistor [tolerance=±5% resistance=4.99k package="0603 [SMD]"]
  R16 = Resistor [tolerance=±5% resistance=15k package="0603 [SMD]"]
  R10 = Resistor [tolerance=±5% resistance=15k package="0603 [SMD]"]
  R8 = Resistor [tolerance=±5% resistance=22k package="0603 [SMD]"]
  R7 = Resistor [tolerance=±5% resistance=470 package="0805 [SMD]"]
  R9 = Resistor [tolerance=±5% resistance=470 package="0805 [SMD]"]
  R14 = Resistor [tolerance=±5% resistance=100 package="0805 [SMD]"]
  R13 = Resistor [tolerance=±5% resistance=100k package="0603 [SMD]"]
  U1 = DIODE-ZENER [package=sod-323]
  L1 = Inductor [current=1.5A inductance=100µH package="400 mil [THT]"]
  LM293D = IC, DIP package, 16 pins [chip_label=LM293]
  LM2576-5 = mystery part, 5 pins [chip_label=?]

nets:
  N1: Raspberry_Pi_B_rev1.3V3, MCP3002.pin8, R8.Pin_1, R7.Pin_1
  N2: Raspberry_Pi_B_rev1.5V, LM386.V+, C2.+, L1.pin_1, LM293D.pin16, LM2576-5.pin4
  N3: Raspberry_Pi_B_rev1.GPIO_3, S1.Pin_2, LEDSW.pin1
  GND: Raspberry_Pi_B_rev1.GND, S1.Pin_3, S1.Pin_4, Q1.E, Q1.K, LED2.cathode, C1.-, AMPIN.pin2, LM386.V-, IRSEN.pin1, MCP3002.pin4, AMPOUT.pin2, LEDSW.pin2, Power_plug1.GND, C2.-, R11.Pin_1, R14.Pin_0, U1.C, LM293D.pin1, LM293D.pin2, LM293D.pin3, LM293D.pin4, LM293D.pin5, LM293D.pin6, LM293D.pin7, LM293D.pin12, LM293D.pin13, LM2576-5.pin3, LM2576-5.pin5
  N4: Raspberry_Pi_B_rev1.GPIO_27, LM293D.pin10
  N5: Raspberry_Pi_B_rev1.GPIO_22, LM293D.pin9
  N6: Raspberry_Pi_B_rev1.GPIO_4, R9.Pin_1
  N7: Raspberry_Pi_B_rev1.GPIO_10, MCP3002.pin5
  N8: Raspberry_Pi_B_rev1.GPIO_9, MCP3002.pin6
  N9: Raspberry_Pi_B_rev1.GPIO_11, MCP3002.pin7
  N10: Raspberry_Pi_B_rev1.GPIO_8, MCP3002.pin1
  N11: Raspberry_Pi_B_rev1.GPIO_7, LM293D.pin15
  N12: M1.pin_1, MOTOR.pin2, LM293D.pin14
  N13: M1.pin_2, MOTOR.pin1, LM293D.pin11
  N14: Q1.A, IRSEN.pin2, R7.Pin_0
  N15: Q1.C, IRSEN.pin3, MCP3002.pin2, R8.Pin_0
  N16: LED2.anode, LEDSW.pin3, R9.Pin_0
  N17: R12.Pin_0, D2.C, C1.+, Power_plug1.VCC
  N18: R12.Pin_1, R10.Pin_0, LM293D.pin8
  N19: D2.A, LM2576-5.pin1
  N20: AMPIN.pin1, R13.Pin_1
  N21: C3.0, LM386.+IN, C8.0, R16.Pin_1
  N22: C3.1, R13.Pin_0
  N23: C4.-, LM386.-IN, C8.1, R16.Pin_0
  N24: C4.+, LM386.BP
  N25: LM386.GAIN, C7.+, R15.Pin_1
  N26: LM386.OUT, C6.0, C5.+
  N27: MCP3002.pin3, R11.Pin_0, R10.Pin_1
  N28: AMPOUT.pin1, C5.-
  N29: C6.1, R14.Pin_1
  N30: C7.-, R15.Pin_0
  N31: U1.A, L1.pin_0, LM2576-5.pin2

notes:
  PB.v9
