# Fritzing sketch pcb_geared_dc (saved by Fritzing 0.8.5b)
circuit board: 4.21539cm x 4.41947cm
breadboards: 2

parts:
  J1 = male pin header, 3 pins [form="♂ (male)"]
  A2D = IC, DIP package, 8 pins [chip_label=MCP3002]
  R2 = Resistor [tolerance=±5% resistance=22k package=THT]
  X2 = USB Connectors [package=usb-a-h]
  R1 = Resistor [tolerance=±5% resistance=470 package=THT]
  Raspberry_Pi_B_rev1 = Raspberry Pi B rev2
  pwr = Power plug
  S1 = Pushbutton [package="[SMD]"]
  LED1 = LED - 5mm [color="Red (633nm)" package="5 mm [THT]"]
  R3 = Resistor [tolerance=±5% resistance=220 package=THT]
  LM293 = IC, DIP package, 16 pins [chip_label=LM293]
  M1 = DC Motor
  Q1 = PHOTOTRANSISTOR REFLECTIVE OBJECT SENSOR [package=qrb1114-side]
  R4 = Resistor [tolerance=±5% resistance=8.2k package=THT]
  R5 = Resistor [tolerance=±5% resistance=8.2k package=THT]
  R6 = Resistor [tolerance=±5% resistance=1 package=THT]

nets:
  GND: J1.pin1, A2D.pin4, X2.GND, Raspberry_Pi_B_rev1.GND, pwr.GND, S1.Pin_3, S1.Pin_4, LED1.cathode, LM293.pin1, LM293.pin4, LM293.pin5, LM293.pin12, LM293.pin13, Q1.E, Q1.K, R5.Pin_1
  N1: J1.pin2, R1.Pin_0, Q1.A
  N2: J1.pin3, A2D.pin2, R2.Pin_0, Q1.C
  N3: A2D.pin1, Raspberry_Pi_B_rev1.GPIO_8
  N4: A2D.pin3, R4.Pin_1, R5.Pin_0
  N5: A2D.pin5, Raspberry_Pi_B_rev1.GPIO_10
  N6: A2D.pin6, Raspberry_Pi_B_rev1.GPIO_9
  N7: A2D.pin7, Raspberry_Pi_B_rev1.GPIO_11
  N8: A2D.pin8, R2.Pin_1, R1.Pin_1, Raspberry_Pi_B_rev1.3V3
  5V: X2.VBUS, Raspberry_Pi_B_rev1.5V, pwr.VCC, LM293.pin16, R6.Pin_1
  N9: Raspberry_Pi_B_rev1.GPIO_3, S1.Pin_1, S1.Pin_2
  N10: Raspberry_Pi_B_rev1.GPIO_27, LM293.pin10
  N11: Raspberry_Pi_B_rev1.GPIO_22, LM293.pin9
  N12: Raspberry_Pi_B_rev1.GPIO_4, R3.Pin_1
  N13: Raspberry_Pi_B_rev1.GPIO_7, LM293.pin15
  N14: LED1.anode, R3.Pin_0
  N15: LM293.pin8, R4.Pin_0, R6.Pin_0
  N16: LM293.pin11, M1.pin_2
  N17: LM293.pin14, M1.pin_1

notes:
  PetBot.v6
