# Fritzing sketch pcb_geared_dc_switching (saved by Fritzing 0.8.7b)
circuit board: 4.21539cm x 4.41947cm
breadboards: 3

parts:
  Raspberry_Pi_B_rev1 = Raspberry Pi B rev2
  S1 = Pushbutton [package="[SMD]"]
  M1 = DC Motor
  Q1 = PHOTOTRANSISTOR REFLECTIVE OBJECT SENSOR [package=qrb1114-side]
  U1 = mystery part, 5 pins [chip_label=?]
  A2D1 = IC, DIP package, 8 pins [chip_label=MCP3002]
  J2 = male pin header, 3 pins [form="♂ (male)"]
  R7 = Resistor [tolerance=±5% resistance=470 package=THT]
  R8 = Resistor [tolerance=±5% resistance=22k package=THT]
  LED2 = LED - 5mm [color="Red (633nm)" package="5 mm [THT]"]
  R9 = Resistor [tolerance=±5% resistance=220 package=THT]
  Power_plug1 = Power plug
  D1 = Schottky Diode [part_number=1N5817 package="Melf DO-213 AB [SMD]"]
  C1 = Electrolytic Capacitor [capacitance=100μF voltage=16V package="100 mil [THT, electrolytic]"]
  C2 = Electrolytic Capacitor [capacitance=1mF package="200 mil [THT, electrolytic]"]
  D2 = Diode [package=diode-1n4001]
  L1 = Inductor [inductance=100µH current=1.5A package="400 mil [THT]"]
  LM294 = IC, DIP package, 16 pins [chip_label=LM293]
  R10 = Resistor [tolerance=±5% resistance=15k package=THT]
  R11 = Resistor [tolerance=±5% resistance=5k package=THT]
  R12 = Resistor [tolerance=±5% resistance=56 power=2W package=THT]
  U2 = LM386 [package=dip08]
  J3 = male pin header, 2 pins [form="♂ (male)"]
  R13 = Resistor [tolerance=±5% resistance=100k package=THT]
  C3 = Ceramic Capacitor [capacitance=100nF package="100 mil [THT, multilayer]"]
  C4 = Electrolytic Capacitor [capacitance=1µF package="100 mil [THT, electrolytic]"]
  C5 = Electrolytic Capacitor [capacitance=1µF package="100 mil [THT, electrolytic]"]
  C6 = Ceramic Capacitor [capacitance=100nF package="100 mil [THT, multilayer]"]
  R14 = Resistor [tolerance=±5% resistance=100 package=THT]
  J4 = male pin header, 2 pins [form="♂ (male)"]

nets:
  N1: Raspberry_Pi_B_rev1.3V3, A2D1.pin8, R7.Pin_1, R8.Pin_1
  N2: Raspberry_Pi_B_rev1.5V, U1.pin4, C2.+, L1.pin_1, LM294.pin16, U2.V+
  N3: Raspberry_Pi_B_rev1.GPIO_3, S1.Pin_1, S1.Pin_2
  GND: Raspberry_Pi_B_rev1.GND, S1.Pin_3, S1.Pin_4, Q1.E, Q1.K, U1.pin3, U1.pin5, A2D1.pin4, J2.pin1, LED2.cathode, Power_plug1.GND, D1.anode, C1.-, C2.-
  N4: Raspberry_Pi_B_rev1.GPIO_27, LM294.pin10
  N5: Raspberry_Pi_B_rev1.GPIO_22, LM294.pin9
  N6: Raspberry_Pi_B_rev1.GPIO_4, R9.Pin_1
  N7: Raspberry_Pi_B_rev1.GPIO_10, A2D1.pin5
  N8: Raspberry_Pi_B_rev1.GPIO_9, A2D1.pin6
  N9: Raspberry_Pi_B_rev1.GPIO_11, A2D1.pin7
  N10: Raspberry_Pi_B_rev1.GPIO_8, A2D1.pin1
  N11: Raspberry_Pi_B_rev1.GPIO_7, LM294.pin15
  N12: M1.pin_1, LM294.pin14
  N13: M1.pin_2, LM294.pin11
  N14: Q1.A, J2.pin2, R7.Pin_0
  N15: Q1.C, A2D1.pin2, J2.pin3, R8.Pin_0
  N16: U1.pin1, D2.A
  N17: U1.pin2, D1.cathode, L1.pin_0
  N18: A2D1.pin3, R10.Pin_1, R11.Pin_0
  N19: LED2.anode, R9.Pin_0
  N20: Power_plug1.VCC, C1.+, D2.C, R12.Pin_0
  N21: LM294.pin8, R10.Pin_0, R12.Pin_1
  N22: LM294.pin12, LM294.pin13, R11.Pin_1, U2.V-, J3.pin2, R14.Pin_0, J4.pin2
  N23: U2.-IN, C4.-
  N24: U2.+IN, C3.0
  N25: U2.OUT, C5.+
  N26: U2.BP, C4.+
  N27: J3.pin1, R13.Pin_1
  N28: R13.Pin_0, C3.1
  N29: C5.-, J4.pin1
  N30: C6.1, R14.Pin_1

notes:
  PetBot.v6
