# Fritzing sketch pcb_geared_dc_switching_v2 (saved by Fritzing 0.8.7b)
breadboards: 3

parts:
  Raspberry_Pi_B_rev1 = Raspberry Pi B rev2
  S1 = Pushbutton [package="[SMD]"]
  M1 = DC Motor
  Q1 = PHOTOTRANSISTOR REFLECTIVE OBJECT SENSOR [package=qrb1114-side]
  LED2 = LED - 5mm [color="Red (633nm)" package="5 mm [THT]"]
  LM294 = IC, DIP package, 16 pins [chip_label=LM293]
  A2D1 = IC, DIP package, 8 pins [chip_label=MCP3002]
  U2 = LM386 [package=dip08]
  Power_plug1 = Power plug
  R12 = Resistor [tolerance=±5% resistance=56 power=2W package=THT]
  D1 = Schottky Diode [part_number=1N5817 package="300 mil [THT]"]
  C2 = Electrolytic Capacitor [capacitance=1mF package="200 mil [THT, electrolytic]"]
  U1 = mystery part, 5 pins [chip_label=?]
  C4 = Electrolytic Capacitor [capacitance=1µF package="100 mil [THT, electrolytic]"]
  C5 = Electrolytic Capacitor [capacitance=1µF package="100 mil [THT, electrolytic]"]
  C1 = Electrolytic Capacitor [capacitance=100μF voltage=16V package="100 mil [THT, electrolytic]"]
  L1 = Inductor [inductance=100µH current=1.5A package="400 mil [THT]"]
  D2 = Diode [package=diode-1n4001]
  R10 = Resistor [tolerance=±5% resistance=15k package=THT]
  R13 = Resistor [tolerance=±5% resistance=100k package=THT]
  C6 = Ceramic Capacitor [capacitance=100nF package="100 mil [THT, multilayer]"]
  R14 = Resistor [tolerance=±5% resistance=100 package=THT]
  C3 = Ceramic Capacitor [capacitance=100nF package="100 mil [THT, multilayer]"]
  AMPIN = male pin header, 2 pins [form="♂ (male)"]
  AMPOUT = male pin header, 2 pins [form="♂ (male)"]
  R8 = Resistor [tolerance=±5% resistance=22k package=THT]
  R7 = Resistor [tolerance=±5% resistance=470 package=THT]
  R11 = Resistor [tolerance=±5% resistance=5k package=THT]
  MOTOR = male pin header, 2 pins [form="♂ (male)"]
  IRSEN = male pin header, 3 pins [form="♂ (male)"]
  R9 = Resistor [tolerance=±5% resistance=220 package=THT]

nets:
  N1: Raspberry_Pi_B_rev1.3V3, A2D1.pin8, R8.Pin_1, R7.Pin_1
  N2: Raspberry_Pi_B_rev1.GPIO_3, S1.Pin_1, S1.Pin_2
  GND: Raspberry_Pi_B_rev1.GND, S1.Pin_3, S1.Pin_4, Q1.E, Q1.K, LED2.cathode, A2D1.pin4, Power_plug1.GND, D1.anode, C2.-, U1.pin3, U1.pin5, C1.-, IRSEN.pin1
  N3: Raspberry_Pi_B_rev1.GPIO_27, LM294.pin10
  N4: Raspberry_Pi_B_rev1.GPIO_22, LM294.pin9
  N5: Raspberry_Pi_B_rev1.GPIO_4, R9.Pin_1
  N6: Raspberry_Pi_B_rev1.GPIO_10, A2D1.pin5
  N7: Raspberry_Pi_B_rev1.GPIO_9, A2D1.pin6
  N8: Raspberry_Pi_B_rev1.GPIO_11, A2D1.pin7
  N9: Raspberry_Pi_B_rev1.GPIO_8, A2D1.pin1
  N10: Raspberry_Pi_B_rev1.GPIO_7, LM294.pin15
  N11: Raspberry_Pi_B_rev1.5V, LM294.pin16, U2.V+, C2.+, U1.pin4, L1.pin_1
  N12: M1.pin_1, LM294.pin14, MOTOR.pin2
  N13: M1.pin_2, LM294.pin11, MOTOR.pin1
  N14: Q1.A, R7.Pin_0, IRSEN.pin2
  N15: Q1.C, A2D1.pin2, R8.Pin_0, IRSEN.pin3
  N16: LED2.anode, R9.Pin_0
  N17: LM294.pin8, R12.Pin_1, R10.Pin_0
  N18: LM294.pin12, LM294.pin13, U2.V-, R14.Pin_0, AMPIN.pin2, AMPOUT.pin2, R11.Pin_1
  N19: A2D1.pin3, R10.Pin_1, R11.Pin_0
  N20: U2.-IN, C4.-
  N21: U2.+IN, C3.0
  N22: U2.OUT, C5.+, C6.0
  N23: U2.BP, C4.+
  N24: Power_plug1.VCC, R12.Pin_0, D2.C
  N25: D1.cathode, U1.pin2, L1.pin_0
  N26: U1.pin1, D2.A
  N27: C5.-, AMPOUT.pin1
  N28: R13.Pin_0, C3.1
  N29: R13.Pin_1, AMPIN.pin1
  N30: C6.1, R14.Pin_1

notes:
  PetBot.v6
