# Fritzing sketch pcb_servo (saved by Fritzing 0.8.5b)
circuit board: 3.76299cm x 3.58423cm
breadboards: 1

parts:
  J1 = male pin header, 3 pins [form="♂ (male)"]
  A2D = IC, DIP package, 8 pins [chip_label=MCP3002]
  R2 = Resistor [tolerance=±5% resistance=22k package=THT]
  X2 = USB Connectors [package=usb-a-h]
  R1 = Resistor [tolerance=±5% resistance=470 package=THT]
  J2 = male pin header, 4 pins [form="♂ (male)"]
  Raspberry_Pi_B_rev1 = Raspberry Pi B rev2
  pwr = Power plug
  S1 = Pushbutton [package="[SMD]"]
  LED1 = LED - 5mm [color="Red (633nm)" package="5 mm [THT]"]
  R3 = Resistor [tolerance=±5% resistance=220 package=THT]

nets:
  GND: J1.pin1, A2D.pin4, X2.GND, J2.pin1, Raspberry_Pi_B_rev1.GND, Raspberry_Pi_B_rev1.GPIO_7, pwr.GND, S1.Pin_1, S1.Pin_2, LED1.cathode
  N1: J1.pin2, R1.Pin_0
  N2: J1.pin3, A2D.pin2, R2.Pin_0
  N3: A2D.pin1, Raspberry_Pi_B_rev1.GPIO_8
  N4: A2D.pin3, J2.pin4
  N5: A2D.pin5, Raspberry_Pi_B_rev1.GPIO_10
  N6: A2D.pin6, Raspberry_Pi_B_rev1.GPIO_9
  N7: A2D.pin7, Raspberry_Pi_B_rev1.GPIO_11
  N8: A2D.pin8, R2.Pin_1, R1.Pin_1, Raspberry_Pi_B_rev1.3V3
  5V: X2.VBUS, J2.pin2, Raspberry_Pi_B_rev1.5V, pwr.VCC
  N9: J2.pin3, Raspberry_Pi_B_rev1.GPIO_25
  N10: Raspberry_Pi_B_rev1.GPIO_2, S1.Pin_4
  N11: Raspberry_Pi_B_rev1.GPIO_4, R3.Pin_1
  N12: LED1.anode, R3.Pin_0

notes:
  PetBot.v5
