# Fritzing sketch pb12 (saved by Fritzing 0.8.7b)
circuit board: 4.55885cm x 7.1999cm
breadboards: 3

parts:
  Raspberry_Pi_B_rev1 = Raspberry Pi B rev2
  S1 = Pushbutton [package="[SMD]"]
  M1 = DC Motor
  R12 = Resistor [tolerance=±5% resistance=6.8 power=2W package=THT]
  A-IN = male pin header, 2 pins [form="♂ (male)"]
  IR = male pin header, 3 pins [form="♂ (male)"]
  A-OUT = male pin header, 2 pins [form="♂ (male)"]
  Power_plug1 = Power plug
  L293 = IC, DIP package, 16 pins [chip_label=L293]
  C5 = Electrolytic Capacitor [capacitance=220µF voltage=10V package="0605 [SMD, electrolytic]"]
  POL5v = mystery part, 3 pins [chip_label=? part_number=OKI-78SR-5/1.5-W36-C]
  C9 = Ceramic Capacitor [capacitance=10µF package="1206 [SMD, multilayer]"]
  MCP3002 = SO08 [chip_label=MCP3002 package=SO]
  C10 = Ceramic Capacitor [capacitance=10µF package="1206 [SMD, multilayer]"]
  LM386 = SO08 [chip_label=IC package=SO]
  R11 = Resistor [tolerance=±5% resistance=4.99k package="0603 [SMD]"]
  R7 = Resistor [tolerance=±5% resistance=150 package="0805 [SMD]"]
  R8 = Resistor [tolerance=±5% resistance=22k package="0603 [SMD]"]
  R15 = Resistor [tolerance=±5% resistance=1k package="0603 [SMD]"]
  R10 = Resistor [tolerance=±5% resistance=15k package="0603 [SMD]"]
  R14 = Resistor [tolerance=±5% resistance=100 package="0805 [SMD]"]
  C8 = Ceramic Capacitor [capacitance=10nF package="0603 [SMD, multilayer]"]
  C6 = Ceramic Capacitor [capacitance=47nF voltage=16V package="0603 [SMD, multilayer]"]
  R16 = Resistor [tolerance=±5% resistance=15k package="0603 [SMD]"]
  R13 = Resistor [tolerance=±5% resistance=100k package="0603 [SMD]"]
  C3 = Ceramic Capacitor [capacitance=100nF package="0603 [SMD, multilayer]"]
  M2 = DC Motor
  LS = male pin header, 5 pins [form="♂ (male)"]
  R18 = Resistor [tolerance=±5% resistance=270 package="0603 [SMD]"]
  R19 = Resistor [tolerance=±5% resistance=270 package="0603 [SMD]"]
  R9 = Resistor [tolerance=±5% resistance=270 package="0603 [SMD]"]
  R21 = Resistor [tolerance=±5% resistance=22k package="0603 [SMD]"]
  5v = Pad [width=1 height=1 connect=center]
  3_3v = Pad [width=1 height=1 connect=center]
  IR_2 = Pad [width=1 height=1 connect=center]
  C11 = Electrolytic Capacitor [capacitance=0.1mF package="0605 [SMD, electrolytic]"]
  D3 = Rectifier Diode [part_number=1N4001 package="300 mil [THT]"]
  Q1 = PHOTOTRANSISTOR REFLECTIVE OBJECT SENSOR [part_number=TCRT5000 package=qrb1114-side]

nets:
  3.3V: Raspberry_Pi_B_rev1.3V3, MCP3002.8, 3_3v.pad
  5V: Raspberry_Pi_B_rev1.5V, L293.pin16, POL5v.pin3, LM386.6, R7.Pin_1, R8.Pin_1, 5v.pad, IR_2.pad, C11.+
  GPIO3: Raspberry_Pi_B_rev1.GPIO_3, S1.Pin_1, S1.Pin_2, LS.pin3
  GND: Raspberry_Pi_B_rev1.GND, S1.Pin_4, A-IN.pin2, IR.pin1, A-OUT.pin2, Power_plug1.GND, L293.pin1, L293.pin4, L293.pin5, L293.pin12, L293.pin13, POL5v.pin2, C9.0, MCP3002.4, LM386.2, LM386.4, R11.Pin_1, R14.Pin_0, C8.1, R16.Pin_0, LS.pin1, C11.-, Q1.E, Q1.K
  GPIO23: Raspberry_Pi_B_rev1.GPIO_23, R18.Pin_0
  GPIO17: Raspberry_Pi_B_rev1.GPIO_17, L293.pin7
  GPIO18: Raspberry_Pi_B_rev1.GPIO_18, L293.pin2
  GPIO27: Raspberry_Pi_B_rev1.GPIO_27, L293.pin10
  GPIO22: Raspberry_Pi_B_rev1.GPIO_22, L293.pin9
  GPIO4: Raspberry_Pi_B_rev1.GPIO_4, R9.Pin_1
  GPIO10: Raspberry_Pi_B_rev1.GPIO_10, MCP3002.5
  GPIO9: Raspberry_Pi_B_rev1.GPIO_9, MCP3002.6
  GPIO25: Raspberry_Pi_B_rev1.GPIO_25, R19.Pin_0
  GPIO11: Raspberry_Pi_B_rev1.GPIO_11, MCP3002.7
  GPIO8: Raspberry_Pi_B_rev1.GPIO_8, MCP3002.1
  GPIO7: Raspberry_Pi_B_rev1.GPIO_7, L293.pin15
  N1: M1.pin_1, L293.pin14
  N2: M1.pin_2, L293.pin11
  12V: R12.Pin_0, Power_plug1.VCC, D3.anode
  N3: R12.Pin_1, L293.pin8, R10.Pin_0
  N4: A-IN.pin1, R13.Pin_1
  N5: IR.pin2, R7.Pin_0, Q1.A
  N6: IR.pin3, R21.Pin_0, Q1.C
  N7: A-OUT.pin1, C5.-
  N8: L293.pin3, M2.pin_1
  N9: L293.pin6, M2.pin_2
  Vout: C5.+, LM386.5, C6.0
  N10: POL5v.pin1, D3.cathode
  N11: C9.1, LM386.7
  AD1: MCP3002.2, R8.Pin_0, R21.Pin_1
  AD2: MCP3002.3, R11.Pin_0, R10.Pin_1
  N12: C10.0, LM386.1
  N13: C10.1, R15.Pin_0
  +IN: LM386.3, C8.0, R16.Pin_1, C3.0
  N14: LM386.8, R15.Pin_1
  N15: R14.Pin_1, C6.1
  N16: R13.Pin_0, C3.1
  N17: LS.pin2, R9.Pin_0
  N18: LS.pin4, R18.Pin_1
  N19: LS.pin5, R19.Pin_1

notes:
  PB.v12
  PetBot, Motor driver
  PetBot, Amplifier for PetBot
  PetBot, LED and switch
  PetBot, Analog to digtial
  PetBot, Raspberry pi
  PetBot, IR sensor
  PetBot, Point of Load
